# Fritzing sketch DeskControl (saved by Fritzing 0.9.4)
circuit board: 6.2cm x 2.7cm
breadboards: 2

parts:
  RJ45 = RJ45 Jack [package=rj45-8]
  WeMos_D1_Mini1 = WeMos D1 Mini
  R6 = Resistor [tolerance=±5% resistance=220 package=THT]
  R4 = Resistor [tolerance=±5% resistance=220 package=THT]
  R5 = Resistor [tolerance=±5% resistance=220 package=THT]
  PC817-D = Sharp PC817 [package=THT]
  R7 = Resistor [tolerance=±5% resistance=220 package=THT]
  PC817-D_2 = Sharp PC817 [package=THT]
  R8 = Resistor [tolerance=±5% resistance=10k package=THT]
  R9 = Resistor [tolerance=±5% resistance=10k package=THT]
  HC-SR04_Sensor_1 = HC-SR04 Ultrasonic Distance Sensor
  J1 = female pin header, 4 pins [form="♀ (female)"]
  LED3 = smd LED [color="Green (555nm)" package="1206 [SMD]"]
  LED4 = smd LED [color="Yellow (585nm)" package="1206 [SMD]"]

nets (from the pcb view):
  N1: RJ45.3, WeMos_D1_Mini1.G, PC817-D.Pin_2, PC817-D_2.Pin_2, HC-SR04_Sensor_1.GND, LED3.cathode, LED4.cathode
  N2: RJ45.7, WeMos_D1_Mini1.D1, R9.Pin_1
  N3: RJ45.8, WeMos_D1_Mini1.D2, R8.Pin_1
  5V: WeMos_D1_Mini1.5V, R8.Pin_0, R9.Pin_0, HC-SR04_Sensor_1.VCC
  N4: WeMos_D1_Mini1.D0, WeMos_D1_Mini1.D3, HC-SR04_Sensor_1.ECHO
  N5: WeMos_D1_Mini1.D5, R4.Pin_1
  N6: WeMos_D1_Mini1.D6, R5.Pin_1
  N7: WeMos_D1_Mini1.D7, R6.Pin_1
  N8: WeMos_D1_Mini1.D8, R7.Pin_1
  N9: R6.Pin_0, LED3.anode
  N10: R4.Pin_0, PC817-D.Pin_1
  N11: R5.Pin_0, PC817-D_2.Pin_1
  N12: PC817-D.Pin_4, J1.pin3
  N13: PC817-D.Pin_3, J1.pin4
  N14: R7.Pin_0, LED4.anode
  N15: PC817-D_2.Pin_4, J1.pin1
  N16: PC817-D_2.Pin_3, J1.pin2

custom parts:
  RJ45 Jack: RJ45 Jack Simple RJ45, 8-pin connection - connector for common Cat5, Cat5e, and Cat6 Ethernet cables. Footprint not yet proven in production. Connector sku is PRT-00643; Breakout PCB sku is BOB-00716.
